// Logisim project B41761-B-2.circ as structural Verilog: 8 circuits, main circuit main
module main (
);

  wire clock_1_out, clock_2_c0, clock_2_c1, clock_2_c2, clock_2_c3, clock_2_c4, controlunit_1_alusrc,
       controlunit_1_memread, controlunit_1_memtoreg, controlunit_1_menwrite, controlunit_1_regdest,
       controlunit_1_regwrite;
  wire [1:0] PCSrc;
  wire [3:0] controlunit_1_aluop;
  wire [4:0] multiplexer_2_out, RT, SA;
  wire [5:0] OpCode;
  wire [10:0] Inst_q_2;
  wire [16:12] Inst_q;
  wire [31:0] adder_1_out, adder_2_out, alu_1_aluresult, bit_extender_1_out, data_memory_1_read_data,
       multiplexer_1_out, multiplexer_3_out, multiplexer_4_out, Op1_q, Op2_q, PC_q, registerfile_1_d1,
       registerfile_1_d2, Result_2_q, Result_q, rom_1_data, shifter_1_out;

  Multiplexer #(.select(2), .width(32), .enable("false")) multiplexer_1 (
    .in0(adder_1_out), .in1(adder_2_out), .in2({adder_1_out[31:22], RT, Inst_q, SA, OpCode, 1'b0}),
    .out(multiplexer_1_out), .sel(PCSrc));  // open: in3
  Clock #(.highDuration(5), .lowDuration(5)) clock_1 (.out(clock_1_out));
  Adder #(.width(32)) adder_1 (.a(32'h4), .b(PC_q), .out(adder_1_out));  // open: cin, cout
  Register #(.width(32)) PC (.D(multiplexer_1_out), .Q(PC_q), .clk(clock_2_c4));  // open: en, clr
  clock clock_2 (
    .clock(clock_1_out), .c0(clock_2_c0), .c1(clock_2_c1), .c2(clock_2_c2), .c3(clock_2_c3), .c4(clock_2_c4));
  Adder #(.width(32)) adder_2 (.a(adder_1_out), .b(shifter_1_out), .out(adder_2_out));  // open: cin, cout
  Register #(.width(32)) Inst (
    .D(rom_1_data), .Q({Inst_q_2, RT, Inst_q, SA, OpCode}), .clk(clock_2_c0));  // open: en, clr
  ROM #(.dataWidth(32)) rom_1 (.addr(PC_q[9:2]), .data(rom_1_data));  // open: sel
  ControlUnit controlunit_1 (
    .Instruction({Inst_q_2, RT, Inst_q, SA, OpCode}), .RegDest(controlunit_1_regdest),
    .RegWrite(controlunit_1_regwrite), .ALUSrc(controlunit_1_alusrc), .MemRead(controlunit_1_memread),
    .MenWrite(controlunit_1_menwrite), .MemToReg(controlunit_1_memtoreg), .ALUOp(controlunit_1_aluop));  // open: Clock, d1
  Multiplexer #(.width(5), .enable("false")) multiplexer_2 (
    .in0(Inst_q), .in1(RT), .out(multiplexer_2_out), .sel(controlunit_1_regdest));
  assign bit_extender_1_out = {{16{Inst_q[16]}}, {Inst_q, SA, OpCode}};  // Bit_Extender bit_extender_1
  RegisterFile registerfile_1 (
    .Clock(clock_2_c4), .d1(registerfile_1_d1), .rs(Inst_q_2[4:0]), .rt(RT), .d2(registerfile_1_d2),
    .Write_register(multiplexer_2_out), .Write_data(Result_2_q), .RegWrite(controlunit_1_regwrite));
  Shifter #(.width(32)) shifter_1 (.in(bit_extender_1_out), .\dist (5'b00010), .out(shifter_1_out));
  Multiplexer #(.width(32), .enable("false")) multiplexer_3 (
    .in0(registerfile_1_d2), .in1(bit_extender_1_out), .out(multiplexer_3_out), .sel(controlunit_1_alusrc));
  Register #(.width(32)) Op1 (.D(registerfile_1_d1), .Q(Op1_q), .clk(clock_2_c1));  // open: en, clr
  Register #(.width(32)) Op2 (.D(multiplexer_3_out), .Q(Op2_q), .clk(clock_2_c1));  // open: en, clr
  ALU alu_1 (
    .Clock(clock_2_c2), .Operand_1(Op1_q), .Operand_2(Op2_q), .ShfAmt(SA), .ALUOp(controlunit_1_aluop),
    .ALUResult(alu_1_aluresult));  // open: Zero, Less_than_zero, Greater_than_zero
  Register #(.width(32)) Result (.D(alu_1_aluresult), .Q(Result_q), .clk(clock_2_c2));  // open: en, clr
  PC_Control pc_control_1 (.ALU_Result(Result_q), .OpCode(OpCode), .RT(RT), .RS_Value(Op1_q), .c0(PCSrc));
  Data_Memory data_memory_1 (
    .Clock(clock_2_c3), .Address(Result_q), .Write_Data(registerfile_1_d2), .MemRead(controlunit_1_memread),
    .MemWrite(controlunit_1_menwrite), .Read_Data(data_memory_1_read_data));
  Multiplexer #(.width(32), .enable("false")) multiplexer_4 (
    .in0(Result_q), .in1(data_memory_1_read_data), .out(multiplexer_4_out), .sel(controlunit_1_memtoreg));
  Register #(.width(32)) Result_2 (.D(multiplexer_4_out), .Q(Result_2_q), .clk(clock_2_c3));  // open: en, clr

  // Notes on the sheet:
  //   contents of rom_1 (hex, n*v repeats v):
  //   20020000 200a0040 5800 8d450000 a03020 200800ff 84600 c83824 10e00005 84202 20420001 1500fffb
  //   214a0001 8000003 ad620000 800000e
  //   R-type
  //   I-type
endmodule

// RefFile
module RegisterFile (
  input  Clock,
  input  [4:0] rs,
  input  [4:0] rt,
  input  [4:0] Write_register,
  input  [31:0] Write_data,
  input  RegWrite,
  output [31:0] d1,
  output [31:0] d2
);

  wire [31:0] demultiplexer_1_out0, demultiplexer_1_out1, demultiplexer_1_out2, demultiplexer_1_out3,
       demultiplexer_1_out4, demultiplexer_1_out5, demultiplexer_1_out6, demultiplexer_1_out7,
       demultiplexer_1_out8, demultiplexer_1_out9, demultiplexer_1_out10, demultiplexer_1_out11,
       demultiplexer_1_out12, demultiplexer_1_out13, demultiplexer_1_out14, demultiplexer_1_out15,
       demultiplexer_1_out16, demultiplexer_1_out17, demultiplexer_1_out18, demultiplexer_1_out19,
       demultiplexer_1_out20, demultiplexer_1_out21, demultiplexer_1_out22, demultiplexer_1_out23,
       demultiplexer_1_out24, demultiplexer_1_out25, demultiplexer_1_out26, demultiplexer_1_out27,
       demultiplexer_1_out28, demultiplexer_1_out29, demultiplexer_1_out30, demultiplexer_1_out31, r0_q,
       r1_q, r2_q, r3_q, r4_q, r5_q, r6_q, r7_q, r8_q, r9_q, r10_q, r11_q, r12_q, r13_q, r14_q, r15_q, r16_q,
       r17_q, r18_q, r19_q, r20_q, r21_q, r22_q, r23_q, r24_q, r25_q, r26_q, r27_q, r28_q, r29_q, r30_q,
       r31_q;

  Demultiplexer #(.select(5), .width(32), .enable("false")) demultiplexer_1 (
    .out0(demultiplexer_1_out0), .out1(demultiplexer_1_out1), .out2(demultiplexer_1_out2),
    .out3(demultiplexer_1_out3), .out4(demultiplexer_1_out4), .out5(demultiplexer_1_out5),
    .out6(demultiplexer_1_out6), .out7(demultiplexer_1_out7), .out8(demultiplexer_1_out8),
    .out9(demultiplexer_1_out9), .out10(demultiplexer_1_out10), .out11(demultiplexer_1_out11),
    .out12(demultiplexer_1_out12), .out13(demultiplexer_1_out13), .out14(demultiplexer_1_out14),
    .out15(demultiplexer_1_out15), .out16(demultiplexer_1_out16), .out17(demultiplexer_1_out17),
    .out18(demultiplexer_1_out18), .out19(demultiplexer_1_out19), .out20(demultiplexer_1_out20),
    .out21(demultiplexer_1_out21), .out22(demultiplexer_1_out22), .out23(demultiplexer_1_out23),
    .out24(demultiplexer_1_out24), .out25(demultiplexer_1_out25), .out26(demultiplexer_1_out26),
    .out27(demultiplexer_1_out27), .out28(demultiplexer_1_out28), .out29(demultiplexer_1_out29),
    .out30(demultiplexer_1_out30), .out31(demultiplexer_1_out31), .in(Write_data), .sel(Write_register));
  Register #(.width(32)) LO ();  // open: D, en, Q, clk, clr
  Register #(.width(32)) HI ();  // open: D, en, Q, clk, clr
  Register #(.width(32)) r0 (.D(demultiplexer_1_out0), .en(RegWrite), .Q(r0_q), .clk(Clock));  // open: clr
  Register #(.width(32)) r8 (.D(demultiplexer_1_out8), .en(RegWrite), .Q(r8_q), .clk(Clock));  // open: clr
  Register #(.width(32)) r16 (.D(demultiplexer_1_out16), .en(RegWrite), .Q(r16_q), .clk(Clock));  // open: clr
  Register #(.width(32)) r24 (.D(demultiplexer_1_out24), .en(RegWrite), .Q(r24_q), .clk(Clock));  // open: clr
  Register #(.width(32)) r1 (.D(demultiplexer_1_out1), .en(RegWrite), .Q(r1_q), .clk(Clock));  // open: clr
  Register #(.width(32)) r9 (.D(demultiplexer_1_out9), .en(RegWrite), .Q(r9_q), .clk(Clock));  // open: clr
  Register #(.width(32)) r17 (.D(demultiplexer_1_out17), .en(RegWrite), .Q(r17_q), .clk(Clock));  // open: clr
  Register #(.width(32)) r25 (.D(demultiplexer_1_out25), .en(RegWrite), .Q(r25_q), .clk(Clock));  // open: clr
  Register #(.width(32)) r2 (.D(demultiplexer_1_out2), .en(RegWrite), .Q(r2_q), .clk(Clock));  // open: clr
  Register #(.width(32)) r10 (.D(demultiplexer_1_out10), .en(RegWrite), .Q(r10_q), .clk(Clock));  // open: clr
  Register #(.width(32)) r18 (.D(demultiplexer_1_out18), .en(RegWrite), .Q(r18_q), .clk(Clock));  // open: clr
  Register #(.width(32)) r26 (.D(demultiplexer_1_out26), .en(RegWrite), .Q(r26_q), .clk(Clock));  // open: clr
  Register #(.width(32)) r3 (.D(demultiplexer_1_out3), .en(RegWrite), .Q(r3_q), .clk(Clock));  // open: clr
  Register #(.width(32)) r11 (.D(demultiplexer_1_out11), .en(RegWrite), .Q(r11_q), .clk(Clock));  // open: clr
  Register #(.width(32)) r19 (.D(demultiplexer_1_out19), .en(RegWrite), .Q(r19_q), .clk(Clock));  // open: clr
  Register #(.width(32)) r27 (.D(demultiplexer_1_out27), .en(RegWrite), .Q(r27_q), .clk(Clock));  // open: clr
  Register #(.width(32)) r4 (.D(demultiplexer_1_out4), .en(RegWrite), .Q(r4_q), .clk(Clock));  // open: clr
  Register #(.width(32)) r12 (.D(demultiplexer_1_out12), .en(RegWrite), .Q(r12_q), .clk(Clock));  // open: clr
  Register #(.width(32)) r20 (.D(demultiplexer_1_out20), .en(RegWrite), .Q(r20_q), .clk(Clock));  // open: clr
  Register #(.width(32)) r28 (.D(demultiplexer_1_out28), .en(RegWrite), .Q(r28_q), .clk(Clock));  // open: clr
  Register #(.width(32)) r5 (.D(demultiplexer_1_out5), .en(RegWrite), .Q(r5_q), .clk(Clock));  // open: clr
  Register #(.width(32)) r13 (.D(demultiplexer_1_out13), .en(RegWrite), .Q(r13_q), .clk(Clock));  // open: clr
  Register #(.width(32)) r21 (.D(demultiplexer_1_out21), .en(RegWrite), .Q(r21_q), .clk(Clock), .clr(Clock));
  Register #(.width(32)) r29 (.D(demultiplexer_1_out29), .en(RegWrite), .Q(r29_q), .clk(Clock));  // open: clr
  Register #(.width(32)) r6 (.D(demultiplexer_1_out6), .en(RegWrite), .Q(r6_q), .clk(Clock));  // open: clr
  Register #(.width(32)) r14 (.D(demultiplexer_1_out14), .en(RegWrite), .Q(r14_q), .clk(Clock));  // open: clr
  Register #(.width(32)) r22 (.D(demultiplexer_1_out22), .en(RegWrite), .Q(r22_q), .clk(Clock), .clr(Clock));
  Register #(.width(32)) r30 (.D(demultiplexer_1_out30), .en(RegWrite), .Q(r30_q), .clk(Clock));  // open: clr
  Register #(.width(32)) r7 (.D(demultiplexer_1_out7), .en(RegWrite), .Q(r7_q), .clk(Clock));  // open: clr
  Register #(.width(32)) r15 (.D(demultiplexer_1_out15), .en(RegWrite), .Q(r15_q), .clk(Clock));  // open: clr
  Register #(.width(32)) r23 (.D(demultiplexer_1_out23), .en(RegWrite), .Q(r23_q), .clr(Clock));  // open: clk
  Register #(.width(32)) r31 (.D(demultiplexer_1_out31), .en(RegWrite), .Q(r31_q), .clk(Clock));  // open: clr
  Multiplexer #(.select(5), .width(32), .enable("false")) multiplexer_1 (
    .in0(r0_q), .in1(r1_q), .in2(r2_q), .in3(r3_q), .in4(r4_q), .in5(r5_q), .in6(r6_q), .in7(r7_q),
    .in8(r8_q), .in9(r9_q), .in10(r10_q), .in11(r11_q), .in12(r12_q), .in13(r13_q), .in14(r14_q),
    .in15(r15_q), .in16(r16_q), .in17(r17_q), .in18(r18_q), .in19(r19_q), .in20(r20_q), .in21(r21_q),
    .in22(r22_q), .in23(r23_q), .in24(r24_q), .in25(r25_q), .in26(r26_q), .in27(r27_q), .in28(r28_q),
    .in29(r29_q), .in30(r30_q), .in31(r31_q), .out(d1), .sel(rs));
  Multiplexer #(.select(5), .width(32), .enable("false")) multiplexer_2 (
    .in0(r0_q), .in1(r1_q), .in2(r2_q), .in3(r3_q), .in4(r4_q), .in5(r5_q), .in6(r6_q), .in7(r7_q),
    .in8(r8_q), .in9(r9_q), .in10(r10_q), .in11(r11_q), .in12(r12_q), .in13(r13_q), .in14(r14_q),
    .in15(r15_q), .in16(r16_q), .in17(r17_q), .in18(r18_q), .in19(r19_q), .in20(r20_q), .in21(r21_q),
    .in22(r22_q), .in23(r23_q), .in24(r24_q), .in25(r25_q), .in26(r26_q), .in27(r27_q), .in28(r28_q),
    .in29(r29_q), .in30(r30_q), .in31(r31_q), .out(d2), .sel(rt));

  // Notes on the sheet:
  //   Entradas
  //   Control
  //   Salidas
endmodule

module ALU (
  input  Clock,
  input  [31:0] Operand_1,
  input  [31:0] Operand_2,
  input  [4:0] ShfAmt,
  input  [3:0] ALUOp,
  output [31:0] ALUResult,
  output Zero,
  output Less_than_zero,
  output Greater_than_zero
);

  wire comparator_1_lt, comparator_2_lt;
  wire [31:0] adder_1_out, adder_2_out, and_1_out, bit_extender_1_out, bit_extender_2_out, divider_1_out,
       nor_1_out, or_1_out, shifter_1_out, shifter_2_out, shifter_3_out, subtractor_1_out, subtractor_2_out,
       xor_1_out;

  Adder #(.width(32)) adder_1 (.a(Operand_1), .b(Operand_1), .out(adder_1_out));  // open: cin, cout
  Adder #(.width(32)) adder_2 (.a(Operand_1), .b(Operand_1), .out(adder_2_out));  // open: cin, cout
  Subtractor #(.width(32)) subtractor_1 (.a(Operand_1), .b(Operand_1), .out(subtractor_1_out));  // open: bin, bout
  Subtractor #(.width(32)) subtractor_2 (.a(Operand_1), .b(Operand_1), .out(subtractor_2_out));  // open: bin, bout
  assign and_1_out = Operand_1 & Operand_1;  // AND_Gate and_1, 32 bits wide
  assign or_1_out = Operand_1 | Operand_1;  // OR_Gate or_1, 32 bits wide
  assign xor_1_out = Operand_1 ^ Operand_2;  // XOR_Gate xor_1, 32 bits wide
  assign nor_1_out = ~(Operand_1 | Operand_2);  // NOR_Gate nor_1, 32 bits wide
  Divider #(.width(32)) divider_1 (.a(Operand_1), .b(Operand_2), .out(divider_1_out));  // open: upper, rem
  Comparator #(.width(32)) comparator_1 (.a(Operand_1), .b(Operand_2), .lt(comparator_1_lt));  // open: gt, eq
  Comparator #(.width(32), .mode("unsigned")) comparator_2 (
    .a(Operand_1), .b(Operand_2), .lt(comparator_2_lt));  // open: gt, eq
  Shifter #(.width(32)) shifter_1 (.in(Operand_2), .\dist (ShfAmt), .out(shifter_1_out));
  Shifter #(.width(32), .shift("lr")) shifter_2 (.in(Operand_2), .\dist (ShfAmt), .out(shifter_2_out));
  Shifter #(.width(32), .shift("ar")) shifter_3 (.in(Operand_2), .\dist (ShfAmt), .out(shifter_3_out));
  assign bit_extender_1_out = {{31{1'b0}}, comparator_1_lt};  // Bit_Extender bit_extender_1
  assign bit_extender_2_out = {{31{1'b0}}, comparator_2_lt};  // Bit_Extender bit_extender_2
  Multiplexer #(.select(4), .width(32), .enable("false")) multiplexer_1 (
    .in0(adder_1_out), .in1(adder_2_out), .in2(subtractor_1_out), .in3(subtractor_2_out), .in5(and_1_out),
    .in6(or_1_out), .in7(xor_1_out), .in8(nor_1_out), .in9(divider_1_out), .in10(bit_extender_1_out),
    .in11(bit_extender_2_out), .in12(shifter_1_out), .in13(shifter_2_out), .in14(shifter_3_out),
    .out(ALUResult), .sel(ALUOp));  // open: in4, in15
  Comparator #(.width(32)) comparator_3 (
    .a(ALUResult), .b({32{1'b0}}), .gt(Less_than_zero), .eq(Zero), .lt(Greater_than_zero));

  // Notes on the sheet:
  //   Entradas
  //   Control
  //   Salidas
endmodule

module clock (
  input  clock,
  output c0,
  output c1,
  output c2,
  output c3,
  output c4
);

  wire [2:0] counter_1_q;

  Demultiplexer #(.select(3), .enable("false")) demultiplexer_1 (
    .out1(c0), .out2(c1), .out3(c2), .out4(c3), .out5(c4), .in(1'b1), .sel(counter_1_q));  // open: out0, out6, out7
  Counter #(.width(3), .max('h5)) counter_1 (.Q(counter_1_q), .clk(clock));  // open: load, D, count, carry, clr

  // Notes on the sheet:
  //   Entradas
  //   Salidas
endmodule

module ControlUnit (
  input  Clock,
  input  [31:0] Instruction,
  output [3:0] d1,
  output RegDest,
  output RegWrite,
  output ALUSrc,
  output MemRead,
  output MenWrite,
  output MemToReg,
  output [3:0] ALUOp
);

  wire comparator_1_eq, comparator_2_eq, comparator_3_eq, comparator_4_eq, comparator_5_eq, comparator_6_lt,
       comparator_7_eq, comparator_7_lt, or_1_out, or_4_out;
  wire [3:0] multiplexer_2_out, multiplexer_3_out, multiplexer_4_out, or_2_out, or_3_out;
  wire [5:0] multiplexer_1_out;

  Comparator #(.width(4)) comparator_1 (.a(Instruction[29:26]), .b(4'b1100), .eq(comparator_1_eq));  // open: gt, lt
  Comparator #(.width(4)) comparator_2 (.a(Instruction[29:26]), .b(4'b1101), .eq(comparator_2_eq));  // open: gt, lt
  Comparator #(.width(4)) comparator_3 (.a(Instruction[29:26]), .b(4'b1110), .eq(comparator_3_eq));  // open: gt, lt
  Comparator #(.width(4)) comparator_4 (.a(Instruction[29:26]), .b(4'b1011), .eq(comparator_4_eq));  // open: gt, lt
  or or_1 (or_1_out, comparator_1_eq, comparator_2_eq, comparator_3_eq, comparator_4_eq);
  Comparator #(.width(6)) comparator_5 (.a({6{1'b0}}), .b(Instruction[31:26]), .eq(comparator_5_eq));  // open: gt, lt
  Comparator #(.width(6)) comparator_6 (.a(Instruction[5:0]), .b(6'b000100), .lt(comparator_6_lt));  // open: gt, eq
  assign or_2_out = Instruction[3:0] | 4'b1100;  // OR_Gate or_2, 4 bits wide
  Multiplexer #(.width(6), .enable("false")) multiplexer_1 (
    .in0({6{1'b0}}), .in1(6'b000001), .out(multiplexer_1_out), .sel(comparator_5_eq));
  assign or_3_out = Instruction[3:0] | 4'b1100;  // OR_Gate or_3, 4 bits wide
  Comparator #(.width(6)) comparator_7 (
    .a(Instruction[5:0]), .b(6'b000011), .eq(comparator_7_eq), .lt(comparator_7_lt));  // open: gt
  Multiplexer #(.width(4), .enable("false")) multiplexer_2 (
    .in0(Instruction[3:0]), .in1(or_2_out), .out(multiplexer_2_out), .sel(comparator_6_lt));
  Multiplexer #(.width(4), .enable("false")) multiplexer_3 (
    .in0(4'b0000), .in1(Instruction[29:26]), .out(multiplexer_3_out), .sel(or_1_out));
  or or_4 (or_4_out, comparator_7_eq, comparator_7_lt);
  Multiplexer #(.select(4), .width(4), .enable("false")) multiplexer_4 (
    .in0(multiplexer_2_out), .in1(4'b0010), .in2(4'b0000), .in4(4'b0010), .in5(4'b0010), .in6(4'b0010),
    .in7(4'b0010), .in8(multiplexer_3_out), .in9(multiplexer_3_out), .in10(multiplexer_3_out),
    .in11(multiplexer_3_out), .in12(multiplexer_3_out), .in13(multiplexer_3_out), .out(multiplexer_4_out),
    .sel(Instruction[29:26]));  // open: in3, in14, in15
  Multiplexer #(.select(3), .width(6), .enable("false")) multiplexer_5 (
    .in0(multiplexer_1_out), .in1(6'b111000), .in4(6'b111101), .in5(6'b101010),
    .out({RegDest, RegWrite, ALUSrc, MemRead, MenWrite, MemToReg}), .sel(Instruction[31:29]));  // open: in2, in3, in6, in7
  Multiplexer #(.width(4), .enable("false")) multiplexer_6 (
    .in0(Instruction[3:0]), .in1(or_3_out), .out(d1), .sel(or_4_out));
  Multiplexer #(.select(2), .width(4), .enable("false")) multiplexer_7 (
    .in0(multiplexer_4_out), .in2(4'b0000), .out(ALUOp), .sel(Instruction[31:30]));  // open: in1, in3

  // Other names for the same wires on the sheet: MemWrite = MenWrite; ALUOp_t[3:0] = d1;
  //   function[5:0] = Instruction[5:0]; CodeH[3:0] = Instruction[29:26]; OpCode[5:0] = Instruction[31:26];
  //   CodeL[1:0] = Instruction[31:30]

  // Notes on the sheet:
  //   Entradas
  //   Salidas
endmodule

module PC_Control (
  input  [31:0] ALU_Result,
  input  [5:0] OpCode,
  input  [4:0] RT,
  input  [31:0] RS_Value,
  output [1:0] c0
);

  wire BEQ_out, BGEZ_out, BGTZ_out, BLEZ_out, BNE_out, comparator_2_eq, comparator_2_gt, comparator_2_lt,
       comparator_3_eq, demultiplexer_1_out1, demultiplexer_1_out4, demultiplexer_1_out5,
       demultiplexer_1_out6, demultiplexer_1_out7, Is_Jump, not_1_out, not_2_out, or_1_out, or_2_out,
       or_3_out;
  wire [0:0] multiplexer_1_out;

  Comparator #(.width(6)) comparator_1 (.a(OpCode), .b(6'b000010), .eq(Is_Jump));  // open: gt, lt
  Comparator #(.width(32)) comparator_2 (
    .a(RS_Value), .b({32{1'b0}}), .gt(comparator_2_gt), .eq(comparator_2_eq), .lt(comparator_2_lt));
  Comparator #(.width(32)) comparator_3 (.a(ALU_Result), .b({32{1'b0}}), .eq(comparator_3_eq));  // open: gt, lt
  Demultiplexer #(.select(3), .enable("false")) demultiplexer_1 (
    .out1(demultiplexer_1_out1), .out4(demultiplexer_1_out4), .out5(demultiplexer_1_out5),
    .out6(demultiplexer_1_out6), .out7(demultiplexer_1_out7), .in(1'b1), .sel(OpCode[2:0]));  // open: out0, out2, out3
  not not_1 (not_1_out, RT[0]);
  not not_2 (not_2_out, comparator_3_eq);
  or or_1 (or_1_out, comparator_2_eq, comparator_2_gt);
  or or_2 (or_2_out, comparator_2_eq, comparator_2_lt);
  and BEQ (BEQ_out, demultiplexer_1_out4, comparator_3_eq);
  and BGEZ (BGEZ_out, RT[0], demultiplexer_1_out1, or_1_out);
  and BGTZ (BGTZ_out, demultiplexer_1_out7, comparator_2_gt);
  and BLEZ (BLEZ_out, demultiplexer_1_out6, or_2_out);
  and BLTZ (BLEZ_out, not_1_out, demultiplexer_1_out1, comparator_2_lt);
  and BNE (BNE_out, demultiplexer_1_out5, not_2_out);
  or or_3 (or_3_out, BGEZ_out, BLEZ_out);
  Multiplexer #(.select(3), .enable("false")) multiplexer_1 (
    .in0(1'b0), .in1(or_3_out), .in2(1'b0), .in3(1'b0), .in4(BEQ_out), .in5(BNE_out), .in6(BLEZ_out),
    .in7(BGTZ_out), .out(multiplexer_1_out[0]), .sel(OpCode[2:0]));
  Multiplexer #(.width(2), .enable("false")) multiplexer_2 (
    .in0({1'b0, multiplexer_1_out[0]}), .in1(2'b10), .out(c0), .sel(Is_Jump));

  // Other names for the same wires on the sheet: BranchCode[2:0] = OpCode[2:0]; PCSrc[1:0] = c0; RTL = RT[0]

  // Notes on the sheet:
  //   Entradas
  //   Salidas
endmodule

module Data_Memory (
  input  Clock,
  input  [31:0] Address,
  input  [31:0] Write_Data,
  input  MemRead,
  input  MemWrite,
  output [31:0] Read_Data
);

  RAM #(.dataWidth(32), .bus("separate")) ram_1 (
    .addr(Address[7:0]), .din(Write_Data), .data(Read_Data), .str(MemWrite), .clk(Clock));  // open: sel, ld, clr

  // Notes on the sheet:
  //   Entradas
  //   Salidas
endmodule

module Regi (
  input  Clock,
  input  [4:0] rs,
  input  [4:0] rt,
  input  [4:0] Write_register,
  input  [31:0] Write_data,
  input  RegWrite,
  output [31:0] d1,
  output [31:0] d2
);

  wire undriven_24, undriven_25, undriven_26, undriven_27, undriven_30, undriven_31, undriven_32,
       undriven_33, undriven_35, undriven_36, undriven_37, undriven_38, undriven_41, undriven_42,
       undriven_43, undriven_44, undriven_47, undriven_48, undriven_49, undriven_50, undriven_52,
       undriven_53, undriven_54, undriven_55, undriven_59, undriven_60, undriven_61, undriven_62,
       undriven_64, undriven_65, undriven_66, undriven_67;
  wire [2:0] multiplexer_1_out, undriven, undriven_2, undriven_3;
  wire [31:0] multiplexer_7_out, multiplexer_11_out, multiplexer_13_out, multiplexer_14_out,
       multiplexer_17_out, r0_q, r1_q, r2_q, r3_q, r4_q, r5_q, r6_q, r7_q, r8_q, r9_q, r10_q, r11_q, r12_q,
       r13_q, r14_q, r15_q, r16_q, r17_q, r18_q, r19_q, r20_q, r21_q, r22_q, r23_q, r24_q, r25_q, r26_q,
       r27_q, r28_q, r29_q, r30_q, r31_q, undriven_4, undriven_5, undriven_6, undriven_7, undriven_8,
       undriven_9, undriven_10, undriven_11, undriven_12, undriven_13, undriven_14, undriven_15, undriven_16,
       undriven_17, undriven_18, undriven_19, undriven_20, undriven_21, undriven_22, undriven_23,
       undriven_28, undriven_29, undriven_34, undriven_39, undriven_40, undriven_45, undriven_46,
       undriven_51, undriven_56, undriven_57, undriven_58, undriven_63;

  Multiplexer #(.select(2), .width(3), .enable("false")) multiplexer_1 (
    .in0(undriven_3), .in1(Write_register[2:0]), .in2(undriven), .in3(undriven_2), .out(multiplexer_1_out),
    .sel(Write_register[4:3]));
  Multiplexer #(.select(3), .width(32), .enable("false")) multiplexer_2 (
    .in0(undriven_4), .in1(undriven_5), .in2(undriven_6), .in3(undriven_39), .in4(undriven_7),
    .in5(undriven_8), .in6(undriven_56), .in7(undriven_9), .out(Write_data), .sel(Write_register[2:0]));
  Multiplexer #(.select(3), .width(32), .enable("false")) multiplexer_3 (
    .in0(undriven_22), .in1(undriven_10), .in2(undriven_34), .in3(undriven_11), .in4(undriven_45),
    .in5(undriven_51), .in6(undriven_12), .in7(undriven_63), .out(Write_data), .sel(Write_register[2:0]));
  Multiplexer #(.select(3), .width(32), .enable("false")) multiplexer_4 (
    .in0(undriven_13), .in1(undriven_28), .in2(undriven_14), .in3(undriven_15), .in4(undriven_46),
    .in5(undriven_16), .in6(undriven_57), .in7(undriven_17), .out(Write_data), .sel(Write_register[2:0]));
  Multiplexer #(.select(3), .width(32), .enable("false")) multiplexer_5 (
    .in0(undriven_23), .in1(undriven_29), .in2(undriven_18), .in3(undriven_40), .in4(undriven_19),
    .in5(undriven_20), .in6(undriven_58), .in7(undriven_21), .out(Write_data), .sel(Write_register[2:0]));
  Register #(.width(32)) r0 (.D(undriven_4), .en(undriven_24), .Q(r0_q), .clk(Clock));  // open: clr
  Register #(.width(32)) r8 (.D(undriven_22), .en(undriven_25), .Q(r8_q), .clk(Clock));  // open: clr
  Register #(.width(32)) r16 (.D(undriven_13), .en(undriven_26), .Q(r16_q), .clk(Clock));  // open: clr
  Register #(.width(32)) r24 (.D(undriven_23), .en(undriven_27), .Q(r24_q), .clk(Clock));  // open: clr
  Register #(.width(32)) r1 (.D(undriven_5), .en(undriven_30), .Q(r1_q), .clk(Clock));  // open: clr
  Register #(.width(32)) r9 (.D(undriven_10), .en(undriven_31), .Q(r9_q), .clk(Clock));  // open: clr
  Register #(.width(32)) r17 (.D(undriven_28), .en(undriven_32), .Q(r17_q), .clk(Clock));  // open: clr
  Register #(.width(32)) r25 (.D(undriven_29), .en(undriven_33), .Q(r25_q), .clk(Clock));  // open: clr
  Register #(.width(32)) r2 (.D(undriven_6), .en(undriven_35), .Q(r2_q), .clk(Clock));  // open: clr
  Register #(.width(32)) r10 (.D(undriven_34), .en(undriven_36), .Q(r10_q), .clk(Clock));  // open: clr
  Register #(.width(32)) r18 (.D(undriven_14), .en(undriven_37), .Q(r18_q), .clk(Clock));  // open: clr
  Register #(.width(32)) r26 (.D(undriven_18), .en(undriven_38), .Q(r26_q), .clk(Clock));  // open: clr
  Register #(.width(32)) r3 (.D(undriven_39), .en(undriven_41), .Q(r3_q), .clk(Clock));  // open: clr
  Register #(.width(32)) r11 (.D(undriven_11), .en(undriven_42), .Q(r11_q), .clk(Clock));  // open: clr
  Register #(.width(32)) r19 (.D(undriven_15), .en(undriven_43), .Q(r19_q), .clk(Clock));  // open: clr
  Register #(.width(32)) r27 (.D(undriven_40), .en(undriven_44), .Q(r27_q), .clk(Clock));  // open: clr
  Register #(.width(32)) r4 (.D(undriven_7), .en(undriven_47), .Q(r4_q), .clk(Clock));  // open: clr
  Register #(.width(32)) r12 (.D(undriven_45), .en(undriven_48), .Q(r12_q), .clk(Clock));  // open: clr
  Register #(.width(32)) r20 (.D(undriven_46), .en(undriven_49), .Q(r20_q), .clk(Clock));  // open: clr
  Register #(.width(32)) r28 (.D(undriven_19), .en(undriven_50), .Q(r28_q), .clk(Clock));  // open: clr
  Register #(.width(32)) r5 (.D(undriven_8), .en(undriven_52), .Q(r5_q), .clk(Clock));  // open: clr
  Register #(.width(32)) r13 (.D(undriven_51), .en(undriven_53), .Q(r13_q), .clk(Clock));  // open: clr
  Register #(.width(32)) r21 (.D(undriven_16), .en(undriven_54), .Q(r21_q), .clk(Clock));  // open: clr
  Register #(.width(32)) r29 (.D(undriven_20), .en(undriven_55), .Q(r29_q), .clk(Clock));  // open: clr
  Register #(.width(32)) r6 (.D(undriven_56), .en(undriven_59), .Q(r6_q), .clk(Clock));  // open: clr
  Register #(.width(32)) r14 (.D(undriven_12), .en(undriven_60), .Q(r14_q), .clk(Clock));  // open: clr
  Register #(.width(32)) r22 (.D(undriven_57), .en(undriven_61), .Q(r22_q), .clk(Clock));  // open: clr
  Register #(.width(32)) r30 (.D(undriven_58), .en(undriven_62), .Q(r30_q), .clk(Clock));  // open: clr
  Register #(.width(32)) r7 (.D(undriven_9), .en(undriven_64), .Q(r7_q), .clk(Clock));  // open: clr
  Register #(.width(32)) r15 (.D(undriven_63), .en(undriven_65), .Q(r15_q), .clk(Clock));  // open: clr
  Register #(.width(32)) r23 (.D(undriven_17), .en(undriven_66), .Q(r23_q), .clk(Clock));  // open: clr
  Register #(.width(32)) r31 (.D(undriven_21), .en(undriven_67), .Q(r31_q), .clk(Clock));  // open: clr
  Multiplexer #(.select(3), .enable("false")) multiplexer_6 (
    .in0(undriven_24), .in1(undriven_30), .in2(undriven_35), .in3(undriven_41), .in4(undriven_47),
    .in5(undriven_52), .in6(undriven_59), .in7(undriven_64), .out(RegWrite), .sel(Write_register[2:0]));
  Multiplexer #(.select(3), .width(32), .enable("false")) multiplexer_7 (
    .in0(r0_q), .in1(r1_q), .in2(r2_q), .in3(r3_q), .in4(r4_q), .in5(r5_q), .in6(r6_q), .in7(r7_q),
    .out(multiplexer_7_out), .sel(rs[2:0]));
  Multiplexer #(.select(3), .width(32), .enable("false")) multiplexer_8 (
    .in0(r0_q), .in1(r1_q), .in2(r2_q), .in3(r3_q), .in4(r4_q), .in5(r5_q), .in6(r6_q), .in7(r7_q),
    .out(multiplexer_7_out), .sel(rt[2:0]));
  Multiplexer #(.select(3), .enable("false")) multiplexer_9 (
    .in0(undriven_25), .in1(undriven_31), .in2(undriven_36), .in3(undriven_42), .in4(undriven_48),
    .in5(undriven_53), .in6(undriven_60), .in7(undriven_65), .out(RegWrite), .sel(Write_register[2:0]));
  Multiplexer #(.select(3), .width(32), .enable("false")) multiplexer_10 (
    .in0(r8_q), .in1(r9_q), .in2(r10_q), .in3(r11_q), .in4(r12_q), .in5(r13_q), .in6(r14_q), .in7(r15_q),
    .out(multiplexer_7_out), .sel(rs[2:0]));
  Multiplexer #(.select(3), .width(32), .enable("false")) multiplexer_11 (
    .in0(r8_q), .in1(r9_q), .in2(r10_q), .in3(r11_q), .in4(r12_q), .in5(r13_q), .in6(r14_q), .in7(r15_q),
    .out(multiplexer_11_out), .sel(rt[2:0]));
  Multiplexer #(.select(3), .enable("false")) multiplexer_12 (
    .in0(undriven_26), .in1(undriven_32), .in2(undriven_37), .in3(undriven_43), .in4(undriven_49),
    .in5(undriven_54), .in6(undriven_61), .in7(undriven_66), .out(RegWrite), .sel(Write_register[2:0]));
  Multiplexer #(.select(3), .width(32), .enable("false")) multiplexer_13 (
    .in0(r16_q), .in1(r17_q), .in2(r18_q), .in3(r19_q), .in4(r20_q), .in5(r21_q), .in6(r22_q), .in7(r23_q),
    .out(multiplexer_13_out), .sel(rs[2:0]));
  Multiplexer #(.select(3), .width(32), .enable("false")) multiplexer_14 (
    .in0(r16_q), .in1(r17_q), .in2(r18_q), .in3(r19_q), .in4(r20_q), .in5(r21_q), .in6(r22_q), .in7(r23_q),
    .out(multiplexer_14_out), .sel(rt[2:0]));
  Multiplexer #(.select(3), .enable("false")) multiplexer_15 (
    .in0(undriven_27), .in1(undriven_33), .in2(undriven_38), .in3(undriven_44), .in4(undriven_50),
    .in5(undriven_55), .in6(undriven_62), .in7(undriven_67), .out(RegWrite), .sel(Write_register[2:0]));
  Multiplexer #(.select(3), .width(32), .enable("false")) multiplexer_16 (
    .in0(r24_q), .in1(r25_q), .in2(r26_q), .in3(r27_q), .in4(r28_q), .in5(r29_q), .in6(r30_q), .in7(r31_q),
    .out(multiplexer_13_out), .sel(rs[2:0]));
  Multiplexer #(.select(3), .width(32), .enable("false")) multiplexer_17 (
    .in0(r24_q), .in1(r25_q), .in2(r26_q), .in3(r27_q), .in4(r28_q), .in5(r29_q), .in6(r30_q), .in7(r31_q),
    .out(multiplexer_17_out), .sel(rt[2:0]));
  Multiplexer #(.select(2), .width(32), .enable("false")) multiplexer_18 (
    .in0(multiplexer_7_out), .in1(multiplexer_7_out), .in2(multiplexer_13_out), .in3(multiplexer_13_out),
    .out(d1), .sel(rs[4:3]));
  Multiplexer #(.select(2), .width(32), .enable("false")) multiplexer_19 (
    .in0(multiplexer_7_out), .in1(multiplexer_11_out), .in2(multiplexer_14_out), .in3(multiplexer_17_out),
    .out(d2), .sel(rt[4:3]));
  // also tied to GND on the sheet: {multiplexer_1_out[0], multiplexer_1_out[1], multiplexer_1_out[2]}

  // Other names for the same wires on the sheet: rs1l[2:0] = rs[2:0]; rs1h[1:0] = rs[4:3]; rs2l[2:0] = rt[2:0];
  //   rs2h[1:0] = rt[4:3]; WRL[2:0] = Write_register[2:0]; WRH[1:0] = Write_register[4:3]

  // Notes on the sheet:
  //   Entradas
  //   Control
  //   Salidas
endmodule
