// Logisim project CPU-Single-Cycle_B41761.circ as structural Verilog: 4 circuits, main circuit main
module main (
  input  MemToReg,
  input  ALUSrc,
  input  [3:0] ALUOp,
  input  PCSrc,
  input  MemWrite
);

  wire clock_1_out, clock_2_c0, clock_2_c1, clock_2_c2, clock_2_c3, clock_2_c4;
  wire [31:0] adder_1_out, alu_1_aluresult, bit_extender_1_out, Inst_q, multiplexer_1_out, multiplexer_2_out,
       multiplexer_3_out, PC_q, ram_1_data, registerfile_1_d1, registerfile_1_d2, Result_2_q, Result_q,
       rom_1_data, undriven;

  Multiplexer #(.width(32), .enable("false")) multiplexer_1 (
    .in0(adder_1_out), .in1(undriven), .out(multiplexer_1_out), .sel(PCSrc));
  Clock clock_1 (.out(clock_1_out));
  Adder #(.width(32)) adder_1 (.a(32'h4), .b(PC_q), .out(adder_1_out));  // open: cin, cout
  Register #(.width(32)) PC (.D(multiplexer_1_out), .Q(PC_q), .clk(clock_2_c4));  // open: en, clr
  clock clock_2 (
    .clock(clock_1_out), .c0(clock_2_c0), .c1(clock_2_c1), .c2(clock_2_c2), .c3(clock_2_c3), .c4(clock_2_c4));
  Register #(.width(32)) Inst (.D(rom_1_data), .Q(Inst_q), .clk(clock_2_c0));  // open: en, clr
  ROM #(.dataWidth(32)) rom_1 (.addr(PC_q[9:2]), .data(rom_1_data));  // open: sel
  RegisterFile registerfile_1 (
    .Clock(clock_2_c1), .rs(Inst_q[25:21]), .rt(Inst_q[20:16]), .Write_register(Inst_q[15:11]),
    .Write_data(Result_2_q), .d1(registerfile_1_d1), .d2(registerfile_1_d2));  // open: RegWrite
  assign bit_extender_1_out = {{16{Inst_q[15]}}, Inst_q[15:0]};  // Bit_Extender bit_extender_1
  ALU alu_1 (
    .Clock(clock_2_c2), .Operand_1(registerfile_1_d1), .Operand_2(multiplexer_2_out), .ALUOp(ALUOp),
    .ALUResult(alu_1_aluresult));  // open: ShfAmt, Zero, Less_than_zero, Greater_than_zero
  Multiplexer #(.width(32), .enable("false")) multiplexer_2 (
    .in0(registerfile_1_d2), .in1(bit_extender_1_out), .out(multiplexer_2_out), .sel(ALUSrc));
  Register #(.width(32)) Result (.D(alu_1_aluresult), .Q(Result_q), .clk(clock_2_c2));  // open: en, clr
  RAM #(.dataWidth(32), .bus("separate")) ram_1 (
    .addr(Result_q[7:0]), .din(registerfile_1_d2), .data(ram_1_data), .str(MemWrite), .clk(clock_2_c3));  // open: sel, ld, clr
  Multiplexer #(.width(32), .enable("false")) multiplexer_3 (
    .in0(Result_q), .in1(ram_1_data), .out(multiplexer_3_out), .sel(MemToReg));
  Register #(.width(32)) Result_2 (.D(multiplexer_3_out), .Q(Result_2_q), .clk(clock_2_c3));  // open: en, clr

  // Notes on the sheet:
  //   contents of rom_1 (hex, n*v repeats v):
  //   14bb020
  //   R-type
  //   I-type
endmodule

// RefFile
module RegisterFile (
  input  Clock,
  input  [4:0] rs,
  input  [4:0] rt,
  input  [4:0] Write_register,
  input  [31:0] Write_data,
  input  RegWrite,
  output [31:0] d1,
  output [31:0] d2
);

  wire [31:0] demultiplexer_1_out0, demultiplexer_1_out1, demultiplexer_1_out2, demultiplexer_1_out3,
       demultiplexer_1_out4, demultiplexer_1_out5, demultiplexer_1_out6, demultiplexer_1_out7,
       demultiplexer_1_out8, demultiplexer_1_out9, demultiplexer_1_out10, demultiplexer_1_out11,
       demultiplexer_1_out12, demultiplexer_1_out13, demultiplexer_1_out14, demultiplexer_1_out15,
       demultiplexer_1_out16, demultiplexer_1_out17, demultiplexer_1_out18, demultiplexer_1_out19,
       demultiplexer_1_out20, demultiplexer_1_out21, demultiplexer_1_out22, demultiplexer_1_out23,
       demultiplexer_1_out24, demultiplexer_1_out25, demultiplexer_1_out26, demultiplexer_1_out27,
       demultiplexer_1_out28, demultiplexer_1_out29, demultiplexer_1_out30, demultiplexer_1_out31, r0_q,
       r1_q, r2_q, r3_q, r4_q, r5_q, r6_q, r7_q, r8_q, r9_q, r10_q, r11_q, r12_q, r13_q, r14_q, r15_q, r16_q,
       r17_q, r18_q, r19_q, r20_q, r21_q, r22_q, r23_q, r24_q, r25_q, r26_q, r27_q, r28_q, r29_q, r30_q,
       r31_q;

  Demultiplexer #(.select(5), .width(32), .enable("false")) demultiplexer_1 (
    .out0(demultiplexer_1_out0), .out1(demultiplexer_1_out1), .out2(demultiplexer_1_out2),
    .out3(demultiplexer_1_out3), .out4(demultiplexer_1_out4), .out5(demultiplexer_1_out5),
    .out6(demultiplexer_1_out6), .out7(demultiplexer_1_out7), .out8(demultiplexer_1_out8),
    .out9(demultiplexer_1_out9), .out10(demultiplexer_1_out10), .out11(demultiplexer_1_out11),
    .out12(demultiplexer_1_out12), .out13(demultiplexer_1_out13), .out14(demultiplexer_1_out14),
    .out15(demultiplexer_1_out15), .out16(demultiplexer_1_out16), .out17(demultiplexer_1_out17),
    .out18(demultiplexer_1_out18), .out19(demultiplexer_1_out19), .out20(demultiplexer_1_out20),
    .out21(demultiplexer_1_out21), .out22(demultiplexer_1_out22), .out23(demultiplexer_1_out23),
    .out24(demultiplexer_1_out24), .out25(demultiplexer_1_out25), .out26(demultiplexer_1_out26),
    .out27(demultiplexer_1_out27), .out28(demultiplexer_1_out28), .out29(demultiplexer_1_out29),
    .out30(demultiplexer_1_out30), .out31(demultiplexer_1_out31), .in(Write_data), .sel(Write_register));
  Register #(.width(32)) r0 (.D(demultiplexer_1_out0), .en(RegWrite), .Q(r0_q), .clk(Clock));  // open: clr
  Register #(.width(32)) r8 (.D(demultiplexer_1_out8), .en(RegWrite), .Q(r8_q), .clk(Clock));  // open: clr
  Register #(.width(32)) r16 (.D(demultiplexer_1_out16), .en(RegWrite), .Q(r16_q), .clk(Clock));  // open: clr
  Register #(.width(32)) r24 (.D(demultiplexer_1_out24), .en(RegWrite), .Q(r24_q), .clk(Clock));  // open: clr
  Register #(.width(32)) r1 (.D(demultiplexer_1_out1), .en(RegWrite), .Q(r1_q), .clk(Clock));  // open: clr
  Register #(.width(32)) r9 (.D(demultiplexer_1_out9), .en(RegWrite), .Q(r9_q), .clk(Clock));  // open: clr
  Register #(.width(32)) r17 (.D(demultiplexer_1_out17), .en(RegWrite), .Q(r17_q), .clk(Clock));  // open: clr
  Register #(.width(32)) r25 (.D(demultiplexer_1_out25), .en(RegWrite), .Q(r25_q), .clk(Clock));  // open: clr
  Register #(.width(32)) r2 (.D(demultiplexer_1_out2), .en(RegWrite), .Q(r2_q), .clk(Clock));  // open: clr
  Register #(.width(32)) r10 (.D(demultiplexer_1_out10), .en(RegWrite), .Q(r10_q), .clk(Clock));  // open: clr
  Register #(.width(32)) r18 (.D(demultiplexer_1_out18), .en(RegWrite), .Q(r18_q), .clk(Clock));  // open: clr
  Register #(.width(32)) r26 (.D(demultiplexer_1_out26), .en(RegWrite), .Q(r26_q), .clk(Clock));  // open: clr
  Register #(.width(32)) r3 (.D(demultiplexer_1_out3), .en(RegWrite), .Q(r3_q), .clk(Clock));  // open: clr
  Register #(.width(32)) r11 (.D(demultiplexer_1_out11), .en(RegWrite), .Q(r11_q), .clk(Clock));  // open: clr
  Register #(.width(32)) r19 (.D(demultiplexer_1_out19), .en(RegWrite), .Q(r19_q), .clk(Clock));  // open: clr
  Register #(.width(32)) r27 (.D(demultiplexer_1_out27), .en(RegWrite), .Q(r27_q), .clk(Clock));  // open: clr
  Register #(.width(32)) r4 (.D(demultiplexer_1_out4), .en(RegWrite), .Q(r4_q), .clk(Clock));  // open: clr
  Register #(.width(32)) r12 (.D(demultiplexer_1_out12), .en(RegWrite), .Q(r12_q), .clk(Clock));  // open: clr
  Register #(.width(32)) r20 (.D(demultiplexer_1_out20), .en(RegWrite), .Q(r20_q), .clk(Clock));  // open: clr
  Register #(.width(32)) r28 (.D(demultiplexer_1_out28), .en(RegWrite), .Q(r28_q), .clk(Clock));  // open: clr
  Register #(.width(32)) r5 (.D(demultiplexer_1_out5), .en(RegWrite), .Q(r5_q), .clk(Clock));  // open: clr
  Register #(.width(32)) r13 (.D(demultiplexer_1_out13), .en(RegWrite), .Q(r13_q), .clk(Clock));  // open: clr
  Register #(.width(32)) r21 (.D(demultiplexer_1_out21), .en(RegWrite), .Q(r21_q), .clk(Clock), .clr(Clock));
  Register #(.width(32)) r29 (.D(demultiplexer_1_out29), .en(RegWrite), .Q(r29_q), .clk(Clock));  // open: clr
  Register #(.width(32)) r6 (.D(demultiplexer_1_out6), .en(RegWrite), .Q(r6_q), .clk(Clock));  // open: clr
  Register #(.width(32)) r14 (.D(demultiplexer_1_out14), .en(RegWrite), .Q(r14_q), .clk(Clock));  // open: clr
  Register #(.width(32)) r22 (.D(demultiplexer_1_out22), .en(RegWrite), .Q(r22_q), .clk(Clock), .clr(Clock));
  Register #(.width(32)) r30 (.D(demultiplexer_1_out30), .en(RegWrite), .Q(r30_q), .clk(Clock));  // open: clr
  Register #(.width(32)) r7 (.D(demultiplexer_1_out7), .en(RegWrite), .Q(r7_q), .clk(Clock));  // open: clr
  Register #(.width(32)) r15 (.D(demultiplexer_1_out15), .en(RegWrite), .Q(r15_q), .clk(Clock));  // open: clr
  Register #(.width(32)) r23 (.D(demultiplexer_1_out23), .en(RegWrite), .Q(r23_q), .clr(Clock));  // open: clk
  Register #(.width(32)) r31 (.D(demultiplexer_1_out31), .en(RegWrite), .Q(r31_q), .clk(Clock));  // open: clr
  Multiplexer #(.select(5), .width(32), .enable("false")) multiplexer_1 (
    .in0(r0_q), .in1(r1_q), .in2(r2_q), .in3(r3_q), .in4(r4_q), .in5(r5_q), .in6(r6_q), .in7(r7_q),
    .in8(r8_q), .in9(r9_q), .in10(r10_q), .in11(r11_q), .in12(r12_q), .in13(r13_q), .in14(r14_q),
    .in15(r15_q), .in16(r16_q), .in17(r17_q), .in18(r18_q), .in19(r19_q), .in20(r20_q), .in21(r21_q),
    .in22(r22_q), .in23(r23_q), .in24(r24_q), .in25(r25_q), .in26(r26_q), .in27(r27_q), .in28(r28_q),
    .in29(r29_q), .in30(r30_q), .in31(r31_q), .out(d1), .sel(rs));
  Multiplexer #(.select(5), .width(32), .enable("false")) multiplexer_2 (
    .in0(r0_q), .in1(r1_q), .in2(r2_q), .in3(r3_q), .in4(r4_q), .in5(r5_q), .in6(r6_q), .in7(r7_q),
    .in8(r8_q), .in9(r9_q), .in10(r10_q), .in11(r11_q), .in12(r12_q), .in13(r13_q), .in14(r14_q),
    .in15(r15_q), .in16(r16_q), .in17(r17_q), .in18(r18_q), .in19(r19_q), .in20(r20_q), .in21(r21_q),
    .in22(r22_q), .in23(r23_q), .in24(r24_q), .in25(r25_q), .in26(r26_q), .in27(r27_q), .in28(r28_q),
    .in29(r29_q), .in30(r30_q), .in31(r31_q), .out(d2), .sel(rt));

  // Notes on the sheet:
  //   Entradas
  //   Control
  //   Salidas
endmodule

module ALU (
  input  Clock,
  input  [31:0] Operand_1,
  input  [31:0] Operand_2,
  input  [4:0] ShfAmt,
  input  [3:0] ALUOp,
  output [31:0] ALUResult,
  output Zero,
  output Less_than_zero,
  output Greater_than_zero
);

  wire [3:0] undriven;
  wire [31:0] adder_1_out, adder_2_out, and_1_out, divider_1_out, multiplier_1_out, negator_1_out, nor_1_out,
       not_1_out, or_1_out, shifter_1_out, shifter_2_out, shifter_3_out, subtractor_1_out, xor_1_out;

  assign not_1_out = ~Operand_1;  // NOT_Gate not_1, 32 bits wide
  assign and_1_out = Operand_1 & Operand_2;  // AND_Gate and_1, 32 bits wide
  assign or_1_out = Operand_1 | Operand_2;  // OR_Gate or_1, 32 bits wide
  assign xor_1_out = Operand_1 ^ Operand_2;  // XOR_Gate xor_1, 32 bits wide
  assign nor_1_out = ~(Operand_1 | Operand_2);  // NOR_Gate nor_1, 32 bits wide
  Adder #(.width(32)) adder_1 (.a(Operand_1), .b(Operand_2), .out(adder_1_out));  // open: cin, cout
  Subtractor #(.width(32)) subtractor_1 (.a(Operand_1), .b(Operand_2), .out(subtractor_1_out));  // open: bin, bout
  Multiplier #(.width(32)) multiplier_1 (.a(Operand_1), .b(Operand_2), .out(multiplier_1_out));  // open: cin, cout
  Divider #(.width(32)) divider_1 (.a(Operand_1), .b(Operand_2), .out(divider_1_out));  // open: upper, rem
  Negator #(.width(32)) negator_1 (.in(Operand_1), .out(negator_1_out));
  Adder #(.width(32)) adder_2 (.a(not_1_out), .b(Operand_2), .out(adder_2_out));  // open: cin, cout
  Shifter #(.width(32)) shifter_1 (.in(Operand_1), .\dist (ShfAmt), .out(shifter_1_out));
  Shifter #(.width(32), .shift("lr")) shifter_2 (.in(Operand_1), .\dist (ShfAmt), .out(shifter_2_out));
  Shifter #(.width(32), .shift("lr")) shifter_3 (.in(Operand_1), .\dist (ShfAmt), .out(shifter_3_out));
  Multiplexer #(.select(4), .width(32), .enable("false")) multiplexer_1 (
    .in1(and_1_out), .in2(or_1_out), .in3(xor_1_out), .in4(nor_1_out), .in5(adder_1_out),
    .in8(subtractor_1_out), .in9(multiplier_1_out), .in10(divider_1_out), .in11(negator_1_out),
    .in12(adder_2_out), .in13(shifter_1_out), .in14(shifter_2_out), .in15(shifter_3_out), .out(ALUResult),
    .sel(undriven));  // open: in0, in6, in7
  Comparator #(.width(4)) comparator_1 (
    .a(undriven), .gt(Less_than_zero), .eq(Zero), .lt(Greater_than_zero));  // open: b

  // Notes on the sheet:
  //   Entradas
  //   Control
  //   Salidas
endmodule

module clock (
  input  clock,
  output c0,
  output c1,
  output c2,
  output c3,
  output c4
);


  // Notes on the sheet:
  //   Entradas
  //   Salidas
endmodule
