// Logisim project Tarea1_B41761.circ as structural Verilog
module NOT (
  input  A,
  output X
);

  Transistor transistor_1 (.in(1'b1), .out(X), .gate(A));
  Transistor #(.\type ("n")) transistor_2 (.in(1'b0), .out(X), .gate(A));

  // Notes on the sheet:
  //   NOT gate
  //   Pull-up network
  //   Pull-down network
endmodule

module AND (
  input  A,
  input  B,
  output X
);

  wire transistor_1_out, transistor_5_out, transistor_6_out;

  Transistor #(.\type ("n")) transistor_1 (.in(1'b1), .out(transistor_1_out), .gate(A));
  Transistor #(.\type ("n")) transistor_2 (.in(transistor_1_out), .out(X), .gate(B));
  Transistor transistor_3 (.in(transistor_5_out), .out(X), .gate(A));
  Transistor transistor_4 (.in(transistor_6_out), .out(X), .gate(B));
  Transistor transistor_5 (.in(1'b0), .out(transistor_5_out), .gate(A));
  Transistor transistor_6 (.in(1'b0), .out(transistor_6_out), .gate(B));

  // Notes on the sheet:
  //   AND gate
  //   Pull-up network
  //   Pull-down network
endmodule

module OR (
  input  A,
  input  B,
  output X
);

  wire transistor_1_out, transistor_3_out, transistor_4_out;

  Transistor #(.\type ("n")) transistor_1 (.in(1'b1), .out(transistor_1_out), .gate(A));
  Transistor #(.\type ("n")) transistor_2 (.in(transistor_1_out), .out(X), .gate(A));
  Transistor transistor_3 (.in(1'b0), .out(transistor_3_out), .gate(A));
  Transistor #(.\type ("n")) transistor_4 (.in(1'b1), .out(transistor_4_out), .gate(B));
  Transistor #(.\type ("n")) transistor_5 (.in(transistor_4_out), .out(X), .gate(B));
  Transistor transistor_6 (.in(transistor_3_out), .out(X), .gate(B));

  // Notes on the sheet:
  //   OR gate
  //   Pull-up network
  //   Pull-down network
  //   0
  //   1
  //   1
  //   0
  //   A/B----------
  //   1
  //   0
  //   -------------
  //   1
  //   1
endmodule

module XOR (
  input  A,
  input  B,
  output X
);

  wire transistor_1_out, transistor_3_out, transistor_4_out, transistor_5_out;

  Transistor #(.\type ("n")) transistor_1 (.in(1'b1), .out(transistor_1_out), .gate(A));
  Transistor transistor_2 (.in(transistor_1_out), .out(X), .gate(B));
  Transistor transistor_3 (.in(1'b0), .out(transistor_3_out), .gate(A));
  Transistor #(.\type ("n")) transistor_4 (.in(1'b0), .out(transistor_4_out), .gate(A));
  Transistor transistor_5 (.in(1'b1), .out(transistor_5_out), .gate(A));
  Transistor #(.\type ("n")) transistor_6 (.in(transistor_5_out), .out(X), .gate(B));
  Transistor transistor_7 (.in(transistor_3_out), .out(X), .gate(B));
  Transistor #(.\type ("n")) transistor_8 (.in(transistor_4_out), .out(X), .gate(B));

  // Notes on the sheet:
  //   XOR gate
  //   Pull-up network
  //   Pull-down network
  //   0
  //   1
  //   1
  //   0
  //   A/B----------
  //   1
  //   0
  //   -------------
  //   0
  //   1
endmodule

module Test (
  input  A,
  input  B,
  output X
);

  Transistor transistor_1 (.in(1'b0), .out(X), .gate(A));
  Transistor #(.\type ("n")) transistor_2 (.in(B), .out(X), .gate(A));

  // Notes on the sheet:
  //   AND gate
  //   Pull-up network
  //   Pull-down network
endmodule
