// Logisim project Tarea2_B41761.circ as structural Verilog: 2 circuits, main circuit NOR gate
module NOR_gate (
  input  A,
  input  B,
  output X
);

  wire transistor_1_out, transistor_2_out, transistor_3_out, transistor_7_out, transistor_9_out,
       transistor_10_out, transistor_11_out, transistor_15_out;

  Transistor transistor_1 (.in(1'b0), .out(transistor_1_out), .gate(A));
  Transistor #(.\type ("n")) transistor_2 (.in(1'b0), .out(transistor_2_out), .gate(A));
  Transistor transistor_3 (.in(1'b1), .out(transistor_3_out), .gate(A));
  Transistor transistor_4 (.in(transistor_3_out), .out(X), .gate(B));
  Transistor #(.\type ("n")) transistor_5 (.in(transistor_1_out), .out(X), .gate(B));
  Transistor transistor_6 (.in(transistor_2_out), .out(X), .gate(B));
  Transistor #(.\type ("n")) transistor_7 (.in(X), .out(transistor_7_out), .gate(A));
  Transistor #(.\type ("n")) transistor_8 (.in(transistor_7_out), .out(X), .gate(B));
  Transistor transistor_9 (.in(1'b0), .out(transistor_9_out), .gate(A));
  Transistor #(.\type ("n")) transistor_10 (.in(1'b0), .out(transistor_10_out), .gate(A));
  Transistor transistor_11 (.in(1'b1), .out(transistor_11_out), .gate(A));
  Transistor transistor_12 (.in(transistor_11_out), .out(X), .gate(B));
  Transistor #(.\type ("n")) transistor_13 (.in(transistor_9_out), .out(X), .gate(B));
  Transistor transistor_14 (.in(transistor_10_out), .out(X), .gate(B));
  Transistor #(.\type ("n")) transistor_15 (.in(X), .out(transistor_15_out), .gate(A));
  Transistor #(.\type ("n")) transistor_16 (.in(transistor_15_out), .out(X), .gate(B));

  // Notes on the sheet:
  //   NOR gate
  //   Pull-up network
  //   Pull-down network
  //   A/B
  //   0
  //   1
  //   1
  //   0
  //   ______________
  //   1
  //   0
  //   ______________
  //   0
  //   0
  //   Pull-up network
  //   Pull-down network
endmodule

module Ej_12_8 (
  input  x1,
  input  x2,
  input  x3,
  input  x4,
  output z1,
  output z2,
  output z3,
  output z4,
  output z5,
  output z6,
  output z7
);

  wire and_1_out, and_2_out, and_3_out, and_4_out, and_5_out, and_6_out, and_7_out, and_8_out, and_9_out,
       and_10_out, and_11_out, and_12_out, and_13_out, and_14_out, not_1_out, not_2_out, not_3_out,
       not_4_out, not_5_out, not_6_out, not_7_out, not_8_out, not_9_out, not_10_out, not_11_out, not_12_out,
       not_13_out, not_14_out, not_15_out, not_16_out, not_17_out, not_18_out, not_19_out;

  not not_1 (not_1_out, x2);
  and and_1 (and_1_out, not_1_out, not_2_out, not_3_out);
  not not_2 (not_2_out, x3);
  not not_3 (not_3_out, x4);
  and and_2 (and_2_out, x3, x4);
  and and_3 (and_3_out, x2, x4);
  not not_4 (not_4_out, x3);
  or or_1 (z2, not_4_out, not_5_out);
  not not_5 (not_5_out, x4);
  not not_6 (not_6_out, x2);
  not not_7 (not_7_out, x3);
  and and_4 (and_4_out, not_7_out, not_8_out);
  not not_8 (not_8_out, x4);
  and and_5 (and_5_out, x3, x4);
  not not_9 (not_9_out, x2);
  and and_6 (and_6_out, not_9_out, x3);
  and and_7 (and_7_out, x2, not_10_out);
  not not_10 (not_10_out, x3);
  and and_8 (and_8_out, x2, not_11_out);
  not not_11 (not_11_out, x4);
  not not_12 (not_12_out, x2);
  and and_9 (and_9_out, not_12_out, not_13_out);
  not not_13 (not_13_out, x4);
  and and_10 (and_10_out, x3, not_14_out);
  not not_14 (not_14_out, x4);
  not not_15 (not_15_out, x3);
  not not_16 (not_16_out, x2);
  and and_11 (and_11_out, not_16_out, x4);
  and and_12 (and_12_out, x2, not_17_out);
  not not_17 (not_17_out, x4);
  not not_18 (not_18_out, x2);
  and and_13 (and_13_out, not_18_out, not_19_out);
  not not_19 (not_19_out, x4);
  and and_14 (and_14_out, x2, x4);
  or or_2 (z1, and_1_out, and_2_out, and_3_out, x1);
  or or_3 (z3, not_6_out, and_4_out, and_5_out);
  or or_4 (z4, and_6_out, and_7_out, and_8_out, x1);
  or or_5 (z5, and_9_out, and_10_out);
  or or_6 (z6, not_15_out, and_11_out, and_12_out);
  or or_7 (z7, and_13_out, x3, and_14_out);
endmodule
